// Logisim project 16BitCPU.circ as structural Verilog: 8 circuits, main circuit main
module main (
);

  wire clock_1_out, cpu_1_halt, frontpanelcontroller_1_cpuclk, frontpanelcontroller_1_runhalt, Reset_out,
       RunStop_out, Step_out;
  wire [3:0] cpu_1_aluflags, cpu_1_flags;
  wire [15:0] cpu_1_alua, cpu_1_alub, cpu_1_aluresult, cpu_1_dmaddress, cpu_1_dmdata, cpu_1_imaddress,
       cpu_1_imdata, cpu_1_writeback, IM_data;

  Clock clock_1 (.out(clock_1_out));
  ROM #(.addrWidth(16), .dataWidth(16)) IM (.addr(cpu_1_imaddress), .data(IM_data));
  FrontPanelController frontpanelcontroller_1 (
    .Clk(clock_1_out), .Run(RunStop_out), .Step(Step_out), .Reset(Reset_out), .Halt(cpu_1_halt),
    .CpuClk(frontpanelcontroller_1_cpuclk), .RunHalt(frontpanelcontroller_1_runhalt));
  CPU cpu_1 (
    .CLK(frontpanelcontroller_1_cpuclk), .Reset(Reset_out), .IMDataIn(IM_data), .Halt(cpu_1_halt),
    .IMAddress(cpu_1_imaddress), .IMData(cpu_1_imdata), .DMAddress(cpu_1_dmaddress), .DMData(cpu_1_dmdata),
    .WriteBack(cpu_1_writeback), .Flags(cpu_1_flags), .AluA(cpu_1_alua), .AluB(cpu_1_alub),
    .ALUResult(cpu_1_aluresult), .ALUFlags(cpu_1_aluflags));
  LED led_1 (.in(cpu_1_flags[3]));
  LED led_2 (.in(cpu_1_flags[2]));
  LED led_3 (.in(cpu_1_flags[1]));
  LED led_4 (.in(cpu_1_flags[0]));
  Hex_Digit_Display hex_digit_display_1 (.value(cpu_1_alua[15:12]));  // open: dp
  LED led_5 (.in(cpu_1_halt));
  Hex_Digit_Display hex_digit_display_2 (.value(cpu_1_imaddress[15:12]));  // open: dp
  Hex_Digit_Display hex_digit_display_3 (.value(cpu_1_imaddress[11:8]));  // open: dp
  Hex_Digit_Display hex_digit_display_4 (.value(cpu_1_imdata[15:12]));  // open: dp
  Hex_Digit_Display hex_digit_display_5 (.value(cpu_1_imdata[11:8]));  // open: dp
  Hex_Digit_Display hex_digit_display_6 (.value(cpu_1_alua[11:8]));  // open: dp
  Hex_Digit_Display hex_digit_display_7 (.value(cpu_1_alua[7:4]));  // open: dp
  LED N (.in(cpu_1_aluflags[3]));
  LED Z (.in(cpu_1_aluflags[2]));
  LED C (.in(cpu_1_aluflags[1]));
  LED led_6 (.in(frontpanelcontroller_1_runhalt));
  Button RunStop (.out(RunStop_out));
  Hex_Digit_Display hex_digit_display_8 (.value(cpu_1_imaddress[7:4]));  // open: dp
  Hex_Digit_Display hex_digit_display_9 (.value(cpu_1_imaddress[3:0]));  // open: dp
  Hex_Digit_Display hex_digit_display_10 (.value(cpu_1_imdata[7:4]));  // open: dp
  // Hex_Digit_Display hex_digit_display_11: pin names not known; wires that end beside it: cpu_1_imdata[3:0]
  Hex_Digit_Display hex_digit_display_12 (.value(cpu_1_alua[3:0]));  // open: dp
  LED V (.in(cpu_1_aluflags[0]));
  Button Step (.out(Step_out));
  Hex_Digit_Display hex_digit_display_13 (.value(cpu_1_dmaddress[15:12]));  // open: dp
  Hex_Digit_Display hex_digit_display_14 (.value(cpu_1_dmdata[15:12]));  // open: dp
  Hex_Digit_Display hex_digit_display_15 (.value(cpu_1_writeback[15:12]));  // open: dp
  Hex_Digit_Display hex_digit_display_16 (.value(cpu_1_alub[15:12]));  // open: dp
  Hex_Digit_Display hex_digit_display_17 (.value(cpu_1_aluresult[15:12]));  // open: dp
  Button Reset (.out(Reset_out));
  Hex_Digit_Display hex_digit_display_18 (.value(cpu_1_dmaddress[11:8]));  // open: dp
  Hex_Digit_Display hex_digit_display_19 (.value(cpu_1_dmaddress[7:4]));  // open: dp
  Hex_Digit_Display hex_digit_display_20 (.value(cpu_1_dmdata[11:8]));  // open: dp
  Hex_Digit_Display hex_digit_display_21 (.value(cpu_1_dmdata[7:4]));  // open: dp
  Hex_Digit_Display hex_digit_display_22 (.value(cpu_1_writeback[11:8]));  // open: dp
  Hex_Digit_Display hex_digit_display_23 (.value(cpu_1_writeback[7:4]));  // open: dp
  Hex_Digit_Display hex_digit_display_24 (.value(cpu_1_alub[11:8]));  // open: dp
  Hex_Digit_Display hex_digit_display_25 (.value(cpu_1_alub[7:4]));  // open: dp
  Hex_Digit_Display hex_digit_display_26 (.value(cpu_1_aluresult[11:8]));  // open: dp
  Hex_Digit_Display hex_digit_display_27 (.value(cpu_1_aluresult[7:4]));  // open: dp
  Hex_Digit_Display hex_digit_display_28 (.value(cpu_1_dmaddress[3:0]));  // open: dp
  Hex_Digit_Display hex_digit_display_29 (.value(cpu_1_dmdata[3:0]));  // open: dp
  Hex_Digit_Display hex_digit_display_30 (.value(cpu_1_writeback[3:0]));  // open: dp
  Hex_Digit_Display hex_digit_display_31 (.value(cpu_1_alub[3:0]));  // open: dp
  Hex_Digit_Display hex_digit_display_32 (.value(cpu_1_aluresult[3:0]));  // open: dp

  // Notes on the sheet:
  //   contents of IM (hex, n*v repeats v):
  //   8002 9003 1628 1031 0 600
  //   N  Z  C  V
  //   Latched Flags
  //   HALT
  //   Instruction Memory
  //   alARM
  //   ALU A Input
  //   ALU Flags
  //   Data Memory
  //   WriteBack
  //   ALU B Input
  //   ALU Result
endmodule

module CPU (
  input  CLK,
  input  Reset,
  input  [15:0] IMDataIn,
  output Halt,
  output [15:0] IMAddress,
  output [15:0] IMData,
  output [15:0] DMAddress,
  output [15:0] DMData,
  output [15:0] WriteBack,
  output [3:0] Flags,
  output [15:0] AluA,
  output [15:0] AluB,
  output [15:0] ALUResult,
  output [3:0] ALUFlags
);

  wire CLKin, decodercontroller_1_carry, decodercontroller_1_immediate, decodercontroller_1_memoryoffset,
       decodercontroller_1_movflagsrn, decodercontroller_1_movr7im, decodercontroller_1_regwrite,
       decodercontroller_1_writedm, JMP, or_1_out, WriteFlags;
  wire [1:0] decodercontroller_1_wdselect;
  wire [2:0] Rd, Rm, Rn;
  wire [3:0] multiplexer_6_out, multiplexer_7_out;
  wire [15:0] bit_extender_1_out, instructionfetch_1_pcplus1, multiplexer_1_out, multiplexer_2_out, RD3,
       registerfile8x16_1_rd2;

  and and_1 (CLKin, CLK, ~Halt);  // AND_Gate
  Multiplexer #(.width(16)) multiplexer_1 (
    .in0(ALUResult), .in1({{5{IMDataIn[11]}}, IMDataIn[10:0]}), .out(multiplexer_1_out),
    .sel(decodercontroller_1_movr7im));
  InstructionFetch instructionfetch_1 (
    .Clk(CLKin), .WBBus(multiplexer_1_out), .JMP(JMP), .Reset(Reset), .IMAddress(IMAddress),
    .PCPlus1(instructionfetch_1_pcplus1));
  DecoderController decodercontroller_1 (
    .IMDataIn(IMDataIn), .Flags(Flags), .RegWrite(decodercontroller_1_regwrite),
    .Immediate(decodercontroller_1_immediate), .Rn(Rn), .Rd(Rd), .Rm(Rm),
    .WriteDM(decodercontroller_1_writedm), .MemoryOffSet(decodercontroller_1_memoryoffset), .JMP(JMP),
    .MovR7Im(decodercontroller_1_movr7im), .Carry(decodercontroller_1_carry), .WriteFlags(WriteFlags),
    .WDSelect(decodercontroller_1_wdselect), .MOVFlagsRn(decodercontroller_1_movflagsrn), .HALT(Halt));
  assign bit_extender_1_out = {{12{Flags[3]}}, Flags};  // Bit_Extender bit_extender_1
  Multiplexer #(.select(2), .width(16)) multiplexer_2 (
    .in0(ALUResult), .in1(AluA), .in2(DMData), .in3(bit_extender_1_out), .out(multiplexer_2_out),
    .sel(decodercontroller_1_wdselect));
  Multiplexer #(.width(16)) multiplexer_3 (
    .in0(multiplexer_2_out), .in1({{5{IMDataIn[11]}}, IMDataIn[10:0]}), .out(WriteBack),
    .sel(decodercontroller_1_immediate));
  RegisterFile8x16 registerfile8x16_1 (
    .Reset(Reset), .clk(CLKin), .WD3(WriteBack), .R7(instructionfetch_1_pcplus1),
    .WE3(decodercontroller_1_regwrite), .A1(Rn), .A2(Rm), .A3(Rd), .RD1(AluA), .RD2(registerfile8x16_1_rd2),
    .RD3(RD3));
  Multiplexer #(.width(16)) multiplexer_4 (
    .in0(AluA), .in1(ALUResult), .out(DMAddress), .sel(decodercontroller_1_memoryoffset));
  Multiplexer #(.width(16)) multiplexer_5 (
    .in0(registerfile8x16_1_rd2), .in1({{5{IMDataIn[11]}}, IMDataIn[10:0]}), .out(AluB),
    .sel(decodercontroller_1_immediate));
  Multiplexer #(.width(4)) multiplexer_6 (.in0(IMDataIn[12:9]), .in1(4'b0000), .out(multiplexer_6_out), .sel(or_1_out));
  or or_1 (or_1_out, decodercontroller_1_memoryoffset, JMP);
  DataMemory datamemory_1 (
    .DMAddress(DMAddress), .WE(decodercontroller_1_writedm), .CLK(CLKin), .DMDataIn(RD3), .DMDataOut(DMData));
  ALU alu_1 (
    .CarryIn(decodercontroller_1_carry), .A(AluA), .B(AluB), .ALUOp(multiplexer_6_out), .FlagsNZCV(ALUFlags),
    .Result(ALUResult));
  Multiplexer #(.width(4)) multiplexer_7 (
    .in0(ALUFlags), .in1(AluA[3:0]), .out(multiplexer_7_out), .sel(decodercontroller_1_movflagsrn));
  Register #(.width(4)) LatchedFlags (.D(multiplexer_7_out), .en(WriteFlags), .clk(CLKin), .Q(Flags), .clr(Reset));

  assign IMData = IMDataIn;

  // Other names for the same wires on the sheet: A[15:0] = AluA; B[15:0] = AluB; Result[15:0] = ALUResult

  // Notes on the sheet:
  //   Immediate
  //   Build your CPU here
endmodule

module FrontPanelController (
  input  Clk,
  input  Run,
  input  Step,
  input  Reset,
  input  Halt,
  output CpuClk,
  output RunHalt
);

  wire and_1_out, or_1_out, pull_resistor_1_node, t_ff_1_q;

  T_Flip_Flop t_ff_1 (.T(pull_resistor_1_node), .clk(Run), .Q(t_ff_1_q), .reset(Reset));  // open: Qn, preset
  Pull_Resistor #(.pull(1)) pull_resistor_1 (.node(pull_resistor_1_node));
  or or_1 (or_1_out, t_ff_1_q, Step);
  and and_1 (and_1_out, Clk, t_ff_1_q);
  and and_2 (RunHalt, or_1_out, ~Halt);  // AND_Gate
  Multiplexer multiplexer_1 (.in0(Step), .in1(and_1_out), .out(CpuClk), .sel(t_ff_1_q));
endmodule

module InstructionFetch (
  input  Clk,
  input  [15:0] WBBus,
  input  JMP,
  input  Reset,
  output [15:0] IMAddress,
  output [15:0] PCPlus1
);

  wire [15:0] adder_1_out, multiplexer_1_out;

  Adder #(.width(16)) adder_1 (.a(IMAddress), .b(16'h1), .out(adder_1_out));  // open: cin, cout
  Multiplexer #(.width(16)) multiplexer_1 (.in0(adder_1_out), .in1(WBBus), .out(multiplexer_1_out), .sel(JMP));
  Register #(.width(16)) register_1 (.D(multiplexer_1_out), .clk(Clk), .Q(IMAddress), .clr(Reset));  // open: en
  Adder #(.width(16)) adder_2 (.a(IMAddress), .b(16'h1), .out(PCPlus1));  // open: cin, cout
endmodule

module ALU (
  input  CarryIn,
  input  [15:0] A,
  input  [15:0] B,
  input  [3:0] ALUOp,
  output [3:0] FlagsNZCV,
  output [15:0] Result
);

  wire adder_1_cout, adder_2_cout, and_3_out, comparator_1_eq, comparator_2_eq, multiplexer_2_out,
       nand_1_out, or_3_out, subtractor_1_bout, xor_2_out, xor_4_out;
  wire [7:0] multiplexer_1_out;
  wire [14:0] adder_1_out;
  wire [14:8] multiplexer_1_out_2;
  wire [15:0] and_1_out, divider_1_out, divider_1_rem, multiplier_1_cout, multiplier_1_out, not_1_out,
       or_1_out, shifter_1_out, shifter_2_out, shifter_3_out, shifter_4_out, shifter_5_out, subtractor_1_out,
       xor_1_out, xor_3_out;
  wire [15:15] adder_2_out;

  assign xor_1_out = B ^ {16{ALUOp[0]}};  // XOR_Gate xor_1, 16 bits wide
  xor xor_2 (xor_2_out, CarryIn, ALUOp[0]);
  Adder #(.width(15)) adder_1 (
    .a(A[14:0]), .b(xor_1_out[14:0]), .out(adder_1_out), .cin(xor_2_out), .cout(adder_1_cout));
  Adder #(.width(1)) adder_2 (
    .a(A[15]), .b(xor_1_out[15]), .out(adder_2_out[15]), .cin(adder_1_cout), .cout(adder_2_cout));
  Subtractor #(.width(16)) subtractor_1 (.a(A), .b(B), .out(subtractor_1_out), .bout(subtractor_1_bout));  // open: bin
  Multiplier #(.width(16)) multiplier_1 (.a(A), .b(B), .out(multiplier_1_out), .cout(multiplier_1_cout));  // open: cin
  Divider #(.width(16)) divider_1 (.a(A), .b(B), .out(divider_1_out), .rem(divider_1_rem));  // open: upper
  assign and_1_out = A & B;  // AND_Gate and_1, 16 bits wide
  assign or_1_out = A | B;  // OR_Gate or_1, 16 bits wide
  assign xor_3_out = A ^ B;  // XOR_Gate xor_3, 16 bits wide
  assign not_1_out = ~A;  // NOT_Gate not_1, 16 bits wide
  Shifter #(.width(16)) shifter_1 (.in(A), .\dist (B[3:0]), .out(shifter_1_out));
  Shifter #(.shift("lr"), .width(16)) shifter_2 (.in(A), .\dist (B[3:0]), .out(shifter_2_out));
  Shifter #(.shift("ar"), .width(16)) shifter_3 (.in(A), .\dist (B[3:0]), .out(shifter_3_out));
  Shifter #(.shift("rl"), .width(16)) shifter_4 (.in(A), .\dist (B[3:0]), .out(shifter_4_out));
  Shifter #(.shift("rr"), .width(16)) shifter_5 (.in(A), .\dist (B[3:0]), .out(shifter_5_out));
  Multiplexer #(.select(4), .width(16)) multiplexer_1 (
    .in0({adder_2_out[15], adder_1_out}), .in1(subtractor_1_out), .in2(multiplier_1_out),
    .in3(multiplier_1_cout), .in4(divider_1_out), .in5(divider_1_rem), .in6(and_1_out), .in7(or_1_out),
    .in8(xor_3_out), .in9(not_1_out), .in10(shifter_1_out), .in11(shifter_2_out), .in12(shifter_3_out),
    .in13(shifter_4_out), .in14(shifter_5_out), .in15(subtractor_1_out),
    .out({FlagsNZCV[3], multiplexer_1_out_2, multiplexer_1_out}), .sel(ALUOp));
  nand nand_1 (nand_1_out, ALUOp[0], ALUOp[1], ALUOp[2], ALUOp[3]);
  assign Result = nand_1_out ? {FlagsNZCV[3], multiplexer_1_out_2, multiplexer_1_out} : 16'bz;  // Controlled_Buffer controlled_buffer_1
  nor nor_1 (FlagsNZCV[2], FlagsNZCV[3], multiplexer_1_out_2[14], multiplexer_1_out_2[13], multiplexer_1_out_2[12], multiplexer_1_out_2[11], multiplexer_1_out_2[10], multiplexer_1_out_2[9], multiplexer_1_out_2[8], multiplexer_1_out[7], multiplexer_1_out[6], multiplexer_1_out[5], multiplexer_1_out[4], multiplexer_1_out[3], multiplexer_1_out[2], multiplexer_1_out[1], multiplexer_1_out[0]);
  Multiplexer multiplexer_2 (.in0(adder_2_cout), .in1(subtractor_1_bout), .out(multiplexer_2_out), .sel(ALUOp[0]));
  and and_2 (FlagsNZCV[1], multiplexer_2_out, or_3_out);
  xor xor_4 (xor_4_out, adder_2_cout, adder_1_cout);
  and and_3 (and_3_out, xor_4_out, or_3_out);
  buf or_2 (FlagsNZCV[0], and_3_out);  // OR_Gate
  or or_3 (or_3_out, comparator_1_eq, comparator_2_eq);
  Comparator #(.width(3)) comparator_1 (.a(ALUOp[3:1]), .b(3'b000), .eq(comparator_1_eq));  // open: gt, lt
  Comparator #(.width(4)) comparator_2 (.a(ALUOp), .b(4'b1111), .eq(comparator_2_eq));  // open: gt, lt

  // Notes on the sheet:
  //   N
  //   Borrow
  //   C-1
  //   Cout
  //   Z
  //   C
  //   V
endmodule

module RegisterFile8x16 (
  input  Reset,
  input  clk,
  input  [15:0] WD3,
  input  [15:0] R7,
  input  WE3,
  input  [2:0] A1,
  input  [2:0] A2,
  input  [2:0] A3,
  output [15:0] RD1,
  output [15:0] RD2,
  output [15:0] RD3
);

  wire demultiplexer_1_out0, demultiplexer_1_out1, demultiplexer_1_out2, demultiplexer_1_out3,
       demultiplexer_1_out4, demultiplexer_1_out5, demultiplexer_1_out6, demultiplexer_1_out7;
  wire [15:0] R0_q, R1_q, R2_q, R3_q, R4_q, R5_q, R6_q;

  Demultiplexer #(.select(3)) demultiplexer_1 (
    .out0(demultiplexer_1_out0), .out1(demultiplexer_1_out1), .out2(demultiplexer_1_out2),
    .out3(demultiplexer_1_out3), .out4(demultiplexer_1_out4), .out5(demultiplexer_1_out5),
    .out6(demultiplexer_1_out6), .out7(demultiplexer_1_out7), .in(WE3), .sel(A3));
  Register #(.width(16)) R0 (.D(WD3), .en(demultiplexer_1_out0), .clk(clk), .Q(R0_q), .clr(Reset));
  Register #(.width(16)) R1 (.D(WD3), .en(demultiplexer_1_out1), .clk(clk), .Q(R1_q), .clr(Reset));
  Register #(.width(16)) R2 (.D(WD3), .en(demultiplexer_1_out2), .clk(clk), .Q(R2_q), .clr(Reset));
  Register #(.width(16)) R3 (.D(WD3), .en(demultiplexer_1_out3), .clk(clk), .Q(R3_q), .clr(Reset));
  Register #(.width(16)) R4 (.D(WD3), .en(demultiplexer_1_out4), .clk(clk), .Q(R4_q), .clr(Reset));
  Register #(.width(16)) R5 (.D(WD3), .en(demultiplexer_1_out5), .clk(clk), .Q(R5_q), .clr(Reset));
  Register #(.width(16)) R6 (.D(WD3), .en(demultiplexer_1_out6), .clk(clk), .Q(R6_q), .clr(Reset));
  Multiplexer #(.select(3), .width(16)) multiplexer_1 (
    .in0(R0_q), .in1(R1_q), .in2(R2_q), .in3(R3_q), .in4(R4_q), .in5(R5_q), .in6(R6_q), .in7(R7), .out(RD1),
    .sel(A1));
  Multiplexer #(.select(3), .width(16)) multiplexer_2 (
    .in0(R0_q), .in1(R1_q), .in2(R2_q), .in3(R3_q), .in4(R4_q), .in5(R5_q), .in6(R6_q), .in7(R7), .out(RD2),
    .sel(A2));
  Multiplexer #(.select(3), .width(16)) multiplexer_3 (
    .in0(R0_q), .in1(R1_q), .in2(R2_q), .in3(R3_q), .in4(R4_q), .in5(R5_q), .in6(R6_q), .in7(R7), .out(RD3),
    .sel(A3));
endmodule

module DecoderController (
  input  [15:0] IMDataIn,
  input  [3:0] Flags,
  output RegWrite,
  output Immediate,
  output [2:0] Rn,
  output [2:0] Rd,
  output [2:0] Rm,
  output WriteDM,
  output MemoryOffSet,
  output JMP,
  output MovR7Im,
  output Carry,
  output WriteFlags,
  output [1:0] WDSelect,
  output MOVFlagsRn,
  output HALT
);

  wire and_1_out, and_3_out, and_4_out, and_6_out, and_9_out, and_10_out, and_11_out, nor_1_out, nor_2_out,
       not_1_out;

  and and_1 (and_1_out, nor_2_out, ~IMDataIn[12], IMDataIn[11], ~IMDataIn[9]);  // AND_Gate
  nor nor_1 (nor_1_out, IMDataIn[15], IMDataIn[14], IMDataIn[13], IMDataIn[10], IMDataIn[9]);
  and and_2 (WriteFlags, ~IMDataIn[15], ~IMDataIn[14], IMDataIn[13]);  // AND_Gate
  nor nor_2 (nor_2_out, IMDataIn[15], IMDataIn[14], IMDataIn[13]);
  not not_1 (not_1_out, WriteFlags);
  nor nor_3 (WDSelect[0], not_1_out, nor_1_out);
  and and_3 (and_3_out, ~IMDataIn[9], ~IMDataIn[10], IMDataIn[11], ~IMDataIn[12], ~IMDataIn[13], ~IMDataIn[14], ~IMDataIn[15]);  // AND_Gate
  and and_4 (and_4_out, ~IMDataIn[9], IMDataIn[10], IMDataIn[11], ~IMDataIn[12], ~IMDataIn[13], ~IMDataIn[14], ~IMDataIn[15]);  // AND_Gate
  and and_5 (MemoryOffSet, ~IMDataIn[9], ~IMDataIn[10], ~IMDataIn[11], IMDataIn[12], ~IMDataIn[13], ~IMDataIn[14], ~IMDataIn[15]);  // AND_Gate
  and and_6 (and_6_out, IMDataIn[9], IMDataIn[10], ~IMDataIn[11], IMDataIn[12], ~IMDataIn[13], ~IMDataIn[14], ~IMDataIn[15]);  // AND_Gate
  or or_1 (WDSelect[1], and_4_out, MemoryOffSet, and_6_out);
  and and_7 (HALT, nor_2_out, ~IMDataIn[12], ~IMDataIn[11], IMDataIn[10], IMDataIn[9]);  // AND_Gate
  and and_8 (MOVFlagsRn, IMDataIn[9], IMDataIn[10], IMDataIn[11], ~IMDataIn[12], nor_2_out);  // AND_Gate
  and and_9 (and_9_out, IMDataIn[13], ~IMDataIn[14], ~IMDataIn[15]);  // AND_Gate
  Multiplexer #(.width(3)) multiplexer_1 (.in0(IMDataIn[5:3]), .in1(IMDataIn[14:12]), .out(Rd), .sel(IMDataIn[15]));
  and and_10 (and_10_out, ~IMDataIn[15], IMDataIn[14]);  // AND_Gate
  Multiplexer #(.width(3)) multiplexer_2 (.in0(IMDataIn[8:6]), .in1(3'b111), .out(Rn), .sel(and_10_out));
  and and_11 (and_11_out, IMDataIn[14], ~IMDataIn[15]);  // AND_Gate
  and and_12 (MovR7Im, IMDataIn[14], IMDataIn[15], IMDataIn[13], IMDataIn[12]);
  or or_2 (RegWrite, and_3_out, and_4_out, MemoryOffSet, and_6_out, and_9_out, IMDataIn[15]);
  or or_3 (JMP, and_11_out, MovR7Im);
  and and_13 (Carry, Flags[1], WriteFlags);
  or or_4 (Immediate, IMDataIn[14], IMDataIn[15]);

  assign Rm = IMDataIn[2:0];

  // Notes on the sheet:
  //   Come back
endmodule

module DataMemory (
  input  [15:0] DMAddress,
  input  WE,
  input  CLK,
  input  [15:0] DMDataIn,
  output [15:0] DMDataOut
);

  RAM #(.addrWidth(16), .asyncread("true"), .dataWidth(16)) ram_1 (
    .addr(DMAddress), .we(WE), .oe(1'b1), .clk(CLK), .din(DMDataIn), .dout(DMDataOut));
endmodule
