// Logisim project HW2_1.circ as structural Verilog: 1 circuit, main circuit main
module main (
);

  wire and_1_out, and_2_out, and_3_out, and_4_out, and_5_out, and_6_out, and_7_out, and_8_out, and_9_out,
       and_10_out, dipswitch_1_p1, dipswitch_1_p2, dipswitch_1_p3, dipswitch_1_p4, not_1_out, not_2_out,
       not_3_out, not_4_out, or_1_out, or_2_out;

  not not_1 (not_1_out, dipswitch_1_p1);
  // DipSwitch #(.number(4)) dipswitch_1: pin names not known; wires that end beside it: dipswitch_1_p1, dipswitch_1_p2, dipswitch_1_p3, dipswitch_1_p4
  not not_2 (not_2_out, dipswitch_1_p2);
  not not_3 (not_3_out, dipswitch_1_p3);
  not not_4 (not_4_out, dipswitch_1_p4);
  and and_1 (and_1_out, not_1_out, not_2_out, dipswitch_1_p3, dipswitch_1_p4);
  and and_2 (and_2_out, not_1_out, dipswitch_1_p2, dipswitch_1_p3, not_4_out);
  and and_3 (and_3_out, dipswitch_1_p1, dipswitch_1_p2, dipswitch_1_p3, dipswitch_1_p4);
  and and_4 (and_4_out, dipswitch_1_p1, not_2_out, not_3_out, dipswitch_1_p4);
  and and_5 (and_5_out, dipswitch_1_p1, dipswitch_1_p2, not_3_out, not_4_out);
  and and_6 (and_6_out, not_1_out, not_2_out, not_3_out, not_4_out);
  and and_7 (and_7_out, not_1_out, not_2_out, dipswitch_1_p3);
  and and_8 (and_8_out, not_2_out, dipswitch_1_p3, dipswitch_1_p4);
  and and_9 (and_9_out, not_1_out, dipswitch_1_p2, dipswitch_1_p4);
  and and_10 (and_10_out, dipswitch_1_p2, not_3_out, dipswitch_1_p4);
  or or_1 (or_1_out, and_7_out, and_8_out, and_9_out, and_10_out);
  or or_2 (or_2_out, and_1_out, and_2_out, and_3_out, and_4_out, and_5_out, and_6_out);
  LED led_1 (.in(or_2_out));
  LED led_2 (.in(or_1_out));

  // Notes on the sheet:
  //   A3
  //   A2
  //   NOT
  //   NOT
  //   A3
  //   A2
  //   A1
  //   NOT
  //   A1
  //   A0
  //   NOT
  //   A0
  //   P
  //   D
endmodule
