// Logisim project HW2_2.circ as structural Verilog: 1 circuit, main circuit main
module main (
);

  wire adder_1_cout, adder_2_cout, adder_3_cout, adder_4_cout, and_1_out, and_3_out, and_4_out, not_2_out,
       xor_2_out;
  wire [1:0] dipswitch_1_p2;
  wire [3:0] adder_1_out, and_2_out, multiplexer_1_out, not_1_out, or_1_out, undriven, undriven_2, xor_1_out;

  assign or_1_out = undriven | undriven_2;  // OR_Gate or_1, 4 bits wide
  // DipSwitch #(.number(2)) dipswitch_1: pin names not known; wires that end beside it: dipswitch_1_p2[0], dipswitch_1_p2[1]
  and and_1 (and_1_out, not_1_out[0], not_1_out[1], not_1_out[2], not_1_out[3]);
  // DipSwitch #(.number(4)) dipswitch_2: pin names not known
  assign and_2_out = undriven & undriven_2;  // AND_Gate and_2, 4 bits wide
  assign not_1_out = ~multiplexer_1_out;  // NOT_Gate not_1, 4 bits wide
  LED led_1 (.in(and_1_out));
  // DipSwitch #(.number(4)) dipswitch_3: pin names not known
  Multiplexer #(.select(2), .width(4)) multiplexer_1 (
    .in0(adder_1_out), .in1(adder_1_out), .in2(and_2_out), .in3(or_1_out), .out(multiplexer_1_out),
    .sel(dipswitch_1_p2));
  LED led_2 (.in(multiplexer_1_out[3]));
  LED led_3 (.in(multiplexer_1_out[3]));
  not not_2 (not_2_out, dipswitch_1_p2[1]);
  LED led_4 (.in(multiplexer_1_out[2]));
  LED led_5 (.in(multiplexer_1_out[1]));
  LED led_6 (.in(multiplexer_1_out[0]));
  assign xor_1_out = undriven_2 ^ {4{dipswitch_1_p2[0]}};  // XOR_Gate xor_1, 4 bits wide
  xor xor_2 (xor_2_out, adder_3_cout, adder_4_cout);
  and and_3 (and_3_out, not_2_out, xor_2_out);
  LED led_7 (.in(and_3_out));
  and and_4 (and_4_out, not_2_out, adder_4_cout);
  LED led_8 (.in(and_4_out));
  Adder #(.width(1)) adder_1 (
    .a(undriven[0]), .b(xor_1_out[0]), .out(adder_1_out[0]), .cin(dipswitch_1_p2[0]), .cout(adder_1_cout));
  Adder #(.width(1)) adder_2 (
    .a(undriven[1]), .b(xor_1_out[1]), .out(adder_1_out[1]), .cin(adder_1_cout), .cout(adder_2_cout));
  Adder #(.width(1)) adder_3 (
    .a(undriven[2]), .b(xor_1_out[2]), .out(adder_1_out[2]), .cin(adder_2_cout), .cout(adder_3_cout));
  Adder #(.width(1)) adder_4 (
    .a(undriven[3]), .b(xor_1_out[3]), .out(adder_1_out[3]), .cin(adder_3_cout), .cout(adder_4_cout));

  // Notes on the sheet:
  //   A
  //   ALU
  //   Control
  //   B
  //   Zero
  //   Negative
  //   Result
  //   A
  //   B
  //   Overflow
  //   Carry
endmodule
