// Logisim project HW2_3.circ as structural Verilog: 1 circuit, main circuit main
module main (
);

  wire dipswitch_1_p1, dipswitch_1_p3, dipswitch_1_p4, dipswitch_1_p6, not_1_out, not_2_out, or_1_out;

  // DipSwitch #(.number(4)) dipswitch_1: pin names not known; wires that end beside it: dipswitch_1_p1, dipswitch_1_p1, dipswitch_1_p3, dipswitch_1_p4, dipswitch_1_p4, dipswitch_1_p6, dipswitch_1_p6
  not not_1 (not_1_out, dipswitch_1_p4);
  or or_1 (or_1_out, not_1_out, dipswitch_1_p3);
  LED led_1 (.in(dipswitch_1_p4));
  LED led_2 (.in(or_1_out));
  not not_2 (not_2_out, or_1_out);
  LED led_3 (.in(not_2_out));
  LED led_4 (.in(not_1_out));

  // Notes on the sheet:
  //   N Z C V
  //   HS
  //   LS
  //   HI
  //   LO
endmodule
