// Logisim project HW2_4A.circ as structural Verilog: 1 circuit, main circuit main
module main (
);

  wire and_1_out, and_2_out, and_4_out, and_5_out, button_1_out, clock_1_out, d_ff_2_q, d_ff_2_qn,
       dipswitch_1_sw1, dipswitch_1_sw2, not_1_out, not_2_out, not_3_out, not_4_out, or_1_out, rgbled_1_p2,
       rgbled_2_p1, rgbled_3_p2, rgbled_4_p1, rgbled_5_p1, rgbled_8_p1, xor_1_out;
  wire [1:0] rgbled_1_p1, rgbled_3_p1, rgbled_10_p2, rgbled_12_p2;

  // RGBLED rgbled_1: pin names not known; wires that end beside it: rgbled_1_p1, rgbled_1_p2
  // RGBLED rgbled_2: pin names not known; wires that end beside it: rgbled_2_p1
  // RGBLED rgbled_3: pin names not known; wires that end beside it: rgbled_3_p1, rgbled_3_p2
  DipSwitch #(.number(2)) dipswitch_1 (.sw1(dipswitch_1_sw1), .sw2(dipswitch_1_sw2));
  not not_1 (not_1_out, dipswitch_1_sw1);
  not not_2 (not_2_out, dipswitch_1_sw2);
  // RGBLED rgbled_4: pin names not known; wires that end beside it: rgbled_4_p1
  Button button_1 (.out(button_1_out));
  and and_1 (and_1_out, not_2_out, rgbled_1_p2, d_ff_2_qn);
  and and_2 (and_2_out, not_1_out, rgbled_8_p1, d_ff_2_qn);
  // RGBLED rgbled_5: pin names not known; wires that end beside it: rgbled_5_p1, rgbled_5_p1
  xor xor_1 (xor_1_out, rgbled_1_p2, d_ff_2_q);
  or or_1 (or_1_out, and_1_out, and_2_out);
  Clock clock_1 (.out(clock_1_out));
  not not_3 (not_3_out, rgbled_8_p1);
  and and_3 (rgbled_5_p1, not_3_out, and_5_out);
  // RGBLED rgbled_6: pin names not known
  // RGBLED rgbled_7: pin names not known; wires that end beside it: rgbled_5_p1, rgbled_5_p1
  // RGBLED rgbled_8: pin names not known; wires that end beside it: rgbled_8_p1
  D_Flip_Flop d_ff_1 (
    .D(xor_1_out), .clk(clock_1_out), .Q(rgbled_1_p2), .Qn(rgbled_8_p1), .reset(button_1_out));  // open: preset
  D_Flip_Flop d_ff_2 (
    .D(or_1_out), .clk(clock_1_out), .Q(d_ff_2_q), .Qn(d_ff_2_qn), .reset(button_1_out));  // open: preset
  nor nor_1 (rgbled_4_p1, and_5_out, rgbled_8_p1);
  // RGBLED rgbled_9: pin names not known; wires that end beside it: rgbled_4_p1
  and and_4 (and_4_out, rgbled_8_p1, d_ff_2_q);
  and and_5 (and_5_out, d_ff_2_q, rgbled_1_p2);
  nor nor_2 (rgbled_3_p2, rgbled_1_p2, and_4_out);
  not not_4 (not_4_out, rgbled_1_p2);
  // RGBLED rgbled_10: pin names not known; wires that end beside it: rgbled_3_p2, rgbled_10_p2
  // RGBLED rgbled_11: pin names not known; wires that end beside it: rgbled_2_p1, rgbled_2_p1
  and and_6 (rgbled_2_p1, and_4_out, not_4_out);
  // RGBLED rgbled_12: pin names not known; wires that end beside it: rgbled_1_p2, rgbled_12_p2

  // Notes on the sheet:
  //   T_A
  //   In Order Left
  //   To Right
  //   T_A
  //   T_B
  //   S_1
  //   NOT S_1
  //   S_0
  //   NOT S_0
  //   Reset
  //   S_1'
  //   S_0'
  //   Clock
  //   T_B
  //   T_B
  //   L_B1
  //   L_B0
  //   L_A1
  //   L_A0
  //   T_A
endmodule
