// Logisim project HW2_4B.circ as structural Verilog: 1 circuit, main circuit main
module main (
);

  wire and_1_out, and_2_out, and_3_out, and_4_out, and_5_out, and_6_out, and_7_out, and_8_out, and_9_out,
       and_10_out, and_11_out, and_12_out, and_13_out, and_14_out, and_15_out, and_16_out, button_1_out,
       clock_1_out, d_ff_1_q, d_ff_1_qn, d_ff_2_q, d_ff_2_qn, d_ff_3_q, d_ff_3_qn, dipswitch_1_sw2,
       not_1_out, not_2_out, not_3_out, not_4_out, or_1_out, or_2_out, or_3_out, rgbled_1_p2, rgbled_2_p1,
       rgbled_3_p1, rgbled_3_p2, rgbled_4_p1, rgbled_9_p1;
  wire [1:0] rgbled_1_p1, rgbled_10_p2;

  // RGBLED rgbled_1: pin names not known; wires that end beside it: rgbled_1_p1, rgbled_1_p2
  // RGBLED rgbled_2: pin names not known; wires that end beside it: rgbled_2_p1
  // RGBLED rgbled_3: pin names not known; wires that end beside it: rgbled_3_p1, rgbled_3_p2
  not not_1 (not_1_out, rgbled_3_p2);
  not not_2 (not_2_out, dipswitch_1_sw2);
  DipSwitch #(.number(2)) dipswitch_1 (.sw1(rgbled_3_p2), .sw2(dipswitch_1_sw2));
  // RGBLED rgbled_4: pin names not known; wires that end beside it: rgbled_4_p1
  and and_1 (and_1_out, d_ff_1_qn, d_ff_2_q, d_ff_3_q, not_2_out);
  and and_2 (and_2_out, d_ff_1_q, d_ff_2_qn, d_ff_3_qn);
  and and_3 (and_3_out, d_ff_1_qn, d_ff_2_qn, d_ff_3_q);
  and and_4 (and_4_out, d_ff_1_qn, d_ff_3_q, dipswitch_1_sw2);
  and and_5 (and_5_out, d_ff_1_qn, d_ff_2_q, d_ff_3_qn);
  and and_6 (and_6_out, d_ff_1_qn, d_ff_3_qn, not_1_out);
  and and_7 (and_7_out, d_ff_1_qn, d_ff_2_q, d_ff_3_qn);
  and and_8 (and_8_out, d_ff_1_qn, d_ff_2_q, dipswitch_1_sw2);
  and and_9 (and_9_out, d_ff_1_q, d_ff_2_qn, d_ff_3_qn);
  // RGBLED rgbled_5: pin names not known
  or or_1 (or_1_out, and_1_out, and_2_out);
  or or_2 (or_2_out, and_3_out, and_4_out, and_5_out);
  Button button_1 (.out(button_1_out));
  or or_3 (or_3_out, and_6_out, and_7_out, and_8_out, and_9_out);
  not not_3 (not_3_out, rgbled_9_p1);
  and and_10 (and_10_out, not_3_out, and_14_out);
  // RGBLED rgbled_6: pin names not known; wires that end beside it: and_10_out, and_10_out
  // RGBLED rgbled_7: pin names not known; wires that end beside it: and_10_out, and_10_out
  D_Flip_Flop d_ff_1 (
    .D(or_1_out), .clk(clock_1_out), .Q(d_ff_1_q), .Qn(d_ff_1_qn), .reset(button_1_out));  // open: preset
  D_Flip_Flop d_ff_2 (
    .D(or_2_out), .clk(clock_1_out), .Q(d_ff_2_q), .Qn(d_ff_2_qn), .reset(button_1_out));  // open: preset
  Clock clock_1 (.out(clock_1_out));
  D_Flip_Flop d_ff_3 (
    .D(or_3_out), .clk(clock_1_out), .Q(d_ff_3_q), .Qn(d_ff_3_qn), .reset(button_1_out));  // open: preset
  nor nor_1 (rgbled_4_p1, and_14_out, rgbled_9_p1);
  // RGBLED rgbled_8: pin names not known; wires that end beside it: rgbled_4_p1
  // RGBLED rgbled_9: pin names not known; wires that end beside it: rgbled_9_p1
  and and_11 (and_11_out, d_ff_3_qn, d_ff_1_qn);
  or or_4 (rgbled_9_p1, and_11_out, and_15_out);
  and and_12 (and_12_out, d_ff_1_q, d_ff_2_qn);
  and and_13 (and_13_out, d_ff_1_qn, d_ff_2_q);
  and and_14 (and_14_out, d_ff_1_q, d_ff_3_qn);
  and and_15 (and_15_out, d_ff_2_qn, d_ff_3_q);
  or or_5 (rgbled_1_p2, and_12_out, and_13_out);
  and and_16 (and_16_out, d_ff_1_qn, d_ff_2_qn, d_ff_3_q);
  nor nor_2 (rgbled_3_p1, rgbled_1_p2, and_16_out);
  not not_4 (not_4_out, rgbled_1_p2);
  // RGBLED rgbled_10: pin names not known; wires that end beside it: rgbled_3_p1, rgbled_10_p2
  // RGBLED rgbled_11: pin names not known; wires that end beside it: rgbled_2_p1, rgbled_2_p1
  and and_17 (rgbled_2_p1, and_16_out, not_4_out);
  // RGBLED rgbled_12: pin names not known; wires that end beside it: rgbled_1_p2

  // Notes on the sheet:
  //   T_A
  //   In Order Left
  //   To Right
  //   T_A
  //   NOT T_A
  //   T_B
  //   NOT T_B
  //   S_2
  //   NOT S_2
  //   S_1
  //   NOT S_1
  //   S_0
  //   NOT S_0
  //   T_A
  //   T_B
  //   S_2'
  //   S_1'
  //   Reset
  //   S_0'
  //   T_B
  //   T_B
  //   Clock
  //   S_2
  //   NOT S_2
  //   S_1
  //   NOT S_1
  //   S_0
  //   NOT S_0
  //   L_B1
  //   L_A1
  //   L_A0
  //   L_B0
  //   T_A
endmodule
