// Logisim project HW2_5.circ as structural Verilog: 1 circuit, main circuit main
module main (
);

  wire and_1_out, and_2_out, and_3_out, and_4_out, and_5_out, and_6_out, and_7_out, and_8_out, button_1_out,
       clock_1_out, clock_2_out, d_ff_1_q, d_ff_2_q, d_ff_3_q, d_ff_4_q, nor_1_out, nor_2_out, nor_3_out,
       nor_4_out, nor_5_out, nor_6_out, nor_7_out, nor_8_out, not_1_out, not_2_out, not_3_out, not_4_out,
       not_5_out;

  Clock clock_1 (.out(clock_1_out));
  not not_1 (not_1_out, nor_7_out);
  and and_1 (and_1_out, not_1_out, clock_1_out);
  nor nor_1 (nor_1_out, and_1_out, nor_2_out);
  and and_2 (and_2_out, nor_7_out, clock_1_out);
  nor nor_2 (nor_2_out, nor_1_out, and_2_out);
  LED led_1 (.in(nor_1_out));
  Clock clock_2 (.out(clock_2_out));
  Button button_1 (.out(button_1_out));
  not not_2 (not_2_out, nor_1_out);
  and and_3 (and_3_out, not_2_out, clock_1_out);
  and and_4 (and_4_out, nor_1_out, clock_1_out);
  D_Flip_Flop d_ff_1 (.D(not_4_out), .clk(clock_2_out), .Q(d_ff_1_q), .reset(button_1_out));  // open: Qn, preset
  nor nor_3 (nor_3_out, and_3_out, nor_4_out);
  nor nor_4 (nor_4_out, nor_3_out, and_4_out);
  LED led_2 (.in(d_ff_1_q));
  D_Flip_Flop d_ff_2 (.D(d_ff_1_q), .clk(clock_2_out), .Q(d_ff_2_q), .reset(button_1_out));  // open: Qn, preset
  LED led_3 (.in(nor_3_out));
  not not_3 (not_3_out, nor_3_out);
  LED led_4 (.in(d_ff_2_q));
  and and_5 (and_5_out, not_3_out, clock_1_out);
  and and_6 (and_6_out, nor_3_out, clock_1_out);
  D_Flip_Flop d_ff_3 (.D(d_ff_2_q), .clk(clock_2_out), .Q(d_ff_3_q), .reset(button_1_out));  // open: Qn, preset
  LED led_5 (.in(nor_5_out));
  nor nor_5 (nor_5_out, and_5_out, nor_6_out);
  nor nor_6 (nor_6_out, nor_5_out, and_6_out);
  LED led_6 (.in(d_ff_3_q));
  not not_4 (not_4_out, d_ff_4_q);
  D_Flip_Flop d_ff_4 (.D(d_ff_3_q), .clk(clock_2_out), .Q(d_ff_4_q), .reset(button_1_out));  // open: Qn, preset
  not not_5 (not_5_out, nor_5_out);
  LED led_7 (.in(d_ff_4_q));
  and and_7 (and_7_out, not_5_out, clock_1_out);
  and and_8 (and_8_out, nor_5_out, clock_1_out);
  LED led_8 (.in(nor_7_out));
  nor nor_7 (nor_7_out, and_7_out, nor_8_out);
  nor nor_8 (nor_8_out, nor_7_out, and_8_out);

  // Notes on the sheet:
  //   Clock
  //   D
  //   Q_a
  //   Clock
  //   Reset
  //   Q_b
  //   Q_a
  //   Q_b
  //   Q_c
  //   Q_c
  //   Q_d
  //   Q_d
endmodule
