// Logisim project HW2_6.circ as structural Verilog: 1 circuit, main circuit main
module main (
);

  wire B, Clk, decoder_1_out0, decoder_1_out1, decoder_1_out2, decoder_1_out3, nor_1_out, not_2_out, RegW,
       Reset, Z;
  wire [1:0] Op;
  wire [5:0] adder_1_out, BTA, multiplexer_1_out, register_5_q;
  wire [7:0] adder_2_out, and_1_out, controlled_buffer_1_out, multiplexer_2_out, multiplexer_3_out,
       not_1_out, register_1_q, register_2_q, register_3_q, register_4_q, Result;

  Clock clock_1 (.out(Clk));
  Button button_1 (.out(Reset));
  Decoder #(.select(2)) decoder_1 (
    .out0(decoder_1_out0), .out1(decoder_1_out1), .out2(decoder_1_out2), .out3(decoder_1_out3),
    .sel(BTA[1:0]), .en(RegW));
  Adder #(.width(6)) adder_1 (.a(register_5_q), .b(6'b000001), .out(adder_1_out));  // open: cin, cout
  Register register_1 (.D(Result), .en(decoder_1_out0), .clk(Clk), .Q(register_1_q), .clr(Reset));
  Register register_2 (.D(Result), .en(decoder_1_out1), .clk(Clk), .Q(register_2_q), .clr(Reset));
  Register register_3 (.D(Result), .en(decoder_1_out2), .clk(Clk), .Q(register_3_q), .clr(Reset));
  Register register_4 (.D(Result), .en(decoder_1_out3), .clk(Clk), .Q(register_4_q), .clr(Reset));
  Register #(.width(6)) register_5 (.D(multiplexer_1_out), .clk(Clk), .Q(register_5_q), .clr(Reset));  // open: en
  Multiplexer #(.width(6)) multiplexer_1 (.in0(adder_1_out), .in1(BTA), .out(multiplexer_1_out), .sel(B));
  ROM #(.addrWidth(6)) rom_1 (.addr(register_5_q), .data({Op, BTA}));
  Multiplexer #(.select(2), .width(8)) multiplexer_2 (
    .in0(register_1_q), .in1(register_2_q), .in2(register_3_q), .in3(register_4_q), .out(multiplexer_2_out),
    .sel(BTA[5:4]));
  Multiplexer #(.select(2), .width(8)) multiplexer_3 (
    .in0(register_1_q), .in1(register_2_q), .in2(register_3_q), .in3(register_4_q), .out(multiplexer_3_out),
    .sel(BTA[3:2]));
  LED led_1 (.in(Op[1]));
  LED led_2 (.in(Op[0]));
  Adder adder_2 (.a(multiplexer_2_out), .b(multiplexer_3_out), .out(adder_2_out));  // open: cin, cout
  Hex_Digit_Display hex_digit_display_1 (.value(register_4_q[7:4]));  // open: dp
  Hex_Digit_Display hex_digit_display_2 (.value(register_4_q[3:0]));  // open: dp
  LED led_3 (.in(BTA[5]));
  LED led_4 (.in(BTA[4]));
  LED led_5 (.in(BTA[3]));
  LED led_6 (.in(BTA[2]));
  assign not_1_out = ~multiplexer_2_out;  // NOT_Gate not_1, 8 bits wide
  assign and_1_out = multiplexer_2_out & multiplexer_3_out;  // AND_Gate and_1, 8 bits wide
  LED led_7 (.in(BTA[1]));
  LED led_8 (.in(BTA[0]));
  assign controlled_buffer_1_out = 1'b0 ? and_1_out : 8'bz;  // Controlled_Buffer controlled_buffer_1
  not not_2 (not_2_out, Z);
  Multiplexer #(.select(2), .width(8)) multiplexer_4 (
    .in0(adder_2_out), .in1(and_1_out), .in2(not_1_out), .in3(controlled_buffer_1_out), .out(Result), .sel(Op));
  nor nor_1 (nor_1_out, Result[7], Result[6], Result[5], Result[4], Result[3], Result[2], Result[1], Result[0]);
  Register #(.width(1)) register_6 (.D(nor_1_out), .en(RegW), .clk(Clk), .Q(Z), .clr(Reset));
  and and_2 (B, Op[0], Op[1], not_2_out);
  nand nand_1 (RegW, Op[0], Op[1]);

  // Other names for the same wires on the sheet: Rn[1:0] = BTA[5:4]; Rd[1:0] = BTA[1:0]; Rm[1:0] = BTA[3:2]

  // Notes on the sheet:
  //   Register File
  //   Fetch
  //   r0
  //   r1
  //   r2
  //   r3
  //   contents of rom_1 (hex, n*v repeats v):
  //   90 44 81 15 91 56 43 57 13 17 54 7d 7 2a ca 55 cf
  //   ALU
  //   Decode
endmodule
